# Fritzing sketch frdm_shema8x8 (saved by Fritzing 0.9.3b)
breadboards: 1

parts:
  8x8_LED_Modul_mit_MAX1 = 8x8 LED Modul mit MAX7219 [package=THT]
  8x8_LED_Modul_mit_MAX2 = 8x8 LED Modul mit MAX7219 [package=THT]
  8x8_LED_Modul_mit_MAX3 = 8x8 LED Modul mit MAX7219 [package=THT]
  8x8_LED_Modul_mit_MAX4 = 8x8 LED Modul mit MAX7219 [package=THT]
  FRDM1 = Freescale FRDM KL25Z

nets:
  N1: 8x8_LED_Modul_mit_MAX1.VCC_Eingang, 8x8_LED_Modul_mit_MAX2.VCC_Eingang, 8x8_LED_Modul_mit_MAX3.VCC_Eingang, 8x8_LED_Modul_mit_MAX4.VCC_Eingang, FRDM1.3.3V
  N2: 8x8_LED_Modul_mit_MAX1.GND_Eingang, 8x8_LED_Modul_mit_MAX2.GND_Eingang, 8x8_LED_Modul_mit_MAX3.GND_Eingang, 8x8_LED_Modul_mit_MAX4.GND_Eingang, FRDM1.GND
  N3: 8x8_LED_Modul_mit_MAX1.DIN_Eingang, 8x8_LED_Modul_mit_MAX2.DIN_Eingang, 8x8_LED_Modul_mit_MAX3.DIN_Eingang, 8x8_LED_Modul_mit_MAX4.DIN_Eingang, FRDM1.PTD2
  N4: 8x8_LED_Modul_mit_MAX1.CS_Eingang, FRDM1.PTD5
  N5: 8x8_LED_Modul_mit_MAX1.CLK_Eingang, 8x8_LED_Modul_mit_MAX2.CLK_Eingang, 8x8_LED_Modul_mit_MAX3.CLK_Eingang, 8x8_LED_Modul_mit_MAX4.CLK_Eingang, FRDM1.PTD1
  N6: 8x8_LED_Modul_mit_MAX2.CS_Eingang, FRDM1.PTC13
  N7: 8x8_LED_Modul_mit_MAX3.CS_Eingang, FRDM1.PTC16
  N8: 8x8_LED_Modul_mit_MAX4.CS_Eingang, FRDM1.PTD0

custom parts:
  Freescale FRDM KL25Z: Freescale FRDM razvojni sistem
